# Fritzing sketch 電路圖 (saved by Fritzing 0.9.3b)
breadboards: 1

parts:
  U1 = attiny85 [package=dip]
  R1 = Resistor [tolerance=±5% resistance=10k package=THT]
  R2 = Resistor [tolerance=±5% resistance=10k package=THT]
  T1 = LM35 Temperature Sensor [package="TO92 [THT]"]
  R3 = Resistor [tolerance=±5% resistance=10k package=THT]
  U2 = RELAY-2 [package=relay-g5v]
  D1 = Rectifier Diode [part_number=1N4001 package="300 mil [THT]"]
  S2 = Pushbutton [package="[THT]"]
  S3 = Pushbutton [package="[THT]"]
  元件1 = TM1637
  R4 = Resistor [tolerance=±5% resistance=10k package=THT]
  D2 = Rectifier Diode [part_number=1N4001 package="300 mil [THT]"]
  D3 = Rectifier Diode [part_number=1N4001 package="300 mil [THT]"]

nets:
  N1: U1.Pin_2, R1.Pin_0, S2.Pin_2
  N2: U1.Pin_3, R2.Pin_0, S3.Pin_4
  N3: U1.Pin_4, R1.Pin_1, R2.Pin_1, T1.+Vs, U2.6, U2.9, U2.10, 元件1.VCC, R4.Pin_0
  N4: U1.Pin_5, 元件1.DIO
  N5: U1.Pin_6, 元件1.CLK
  N6: U1.Pin_7, R3.Pin_0
  N7: U1.Pin_8, D3.cathode
  N8: T1.Vout, U2.2, D1.anode
  N9: T1.GND, R3.Pin_1, R4.Pin_1
  N10: D1.cathode, S2.Pin_4, S3.Pin_1, S3.Pin_2, 元件1.GND, D2.anode
  N11: D2.cathode, D3.anode

notes:
  DC 5V
  GND
  5V Relay
  常閉
  1N4007 飛輪
  ATTiny85
  10KΩ
  10KΩ
  2SC1815
  微動開關
  10KΩ
  10KΩ
  AC 110V
  火線 IN
  AC 110V
  火線 OUT
  ATTiny85 倒數計時定時器
  羽山秋人 ( https://3wa.tw )
  2026-02-01
  TM1637 Display
  1N4007 x2
  讓ATTiny85 電壓稍低

custom parts:
  TM1637: A 4 7-seg display
